# Fritzing sketch ArduinoAsProgrammator (saved by Fritzing 0.7.11b)
breadboards: 1

parts:
  Arduino1 = Arduino
  C1 = Electrolytic Capacitor [capacitance=10µF voltage=35V package="100 mil [THT, electrolytic]"]
  IC1 = IC, DIP package, 20 pins [chip_label=ATTiny]
  R1 = Resistor [tolerance=±5% resistance=220 package=THT]
  R2 = Resistor [tolerance=±5% resistance=220 package=THT]
  R3 = Resistor [tolerance=±5% resistance=220 package=THT]
  LED1 = LED - 5mm [color="Blue (505nm)" package="5 mm [THT]"]
  LED2 = LED - 5mm [color="Red (633nm)" package="5 mm [THT]"]
  LED3 = LED - 5mm [color="Green (565nm)" package="5 mm [THT]"]

nets:
  N1: Arduino1.GND, C1.-, IC1.pin10, R1.Pin_1, R2.Pin_1, R3.Pin_1
  N2: Arduino1.D13, IC1.pin19
  N3: Arduino1.D12, IC1.pin18
  N4: Arduino1.D11, IC1.pin17
  N5: Arduino1.D10, IC1.pin1
  N6: Arduino1.D9, LED3.anode
  N7: Arduino1.D8, LED2.anode
  N8: Arduino1.D7, LED1.anode
  N9: Arduino1.RST, C1.+
  N10: Arduino1.+5V, IC1.pin20
  N11: R1.Pin_0, LED1.cathode
  N12: R2.Pin_0, LED2.cathode
  N13: R3.Pin_0, LED3.cathode

notes:
  pin 7 - programming LED
  pin 8 - error LED
  pin 9 - heartbeat LED
  pin 10 - slave reset
  pin 11 - MOSI
  pin 12 - MISO
  pin 13 - SCK
  Arduino scetch - ArduinoISP
